// Logisim project 8-Bit processor.circ as structural Verilog
module _1_bit_MEM (
  input  S,
  input  E,
  output out_3
);

  wire nand_1_out, nand_2_out, nand_4_out;

  nand nand_1 (nand_1_out, S, E);
  nand nand_2 (nand_2_out, E, nand_1_out);
  nand nand_3 (out_3, nand_1_out, nand_4_out);
  nand nand_4 (nand_4_out, out_3, nand_2_out);
endmodule

module _8_bit_MEM (
  input  [7:0] in_1,
  input  in_2,
  output [7:0] out_3
);

  _1_bit_MEM u_1_bit_mem_1 (.S(in_1[0]), .E(in_2), .out_3(out_3[0]));
  _1_bit_MEM u_1_bit_mem_2 (.S(in_1[1]), .E(in_2), .out_3(out_3[1]));
  _1_bit_MEM u_1_bit_mem_3 (.S(in_1[2]), .E(in_2), .out_3(out_3[2]));
  _1_bit_MEM u_1_bit_mem_4 (.S(in_1[3]), .E(in_2), .out_3(out_3[3]));
  _1_bit_MEM u_1_bit_mem_5 (.S(in_1[4]), .E(in_2), .out_3(out_3[4]));
  _1_bit_MEM u_1_bit_mem_6 (.S(in_1[5]), .E(in_2), .out_3(out_3[5]));
  _1_bit_MEM u_1_bit_mem_7 (.S(in_1[6]), .E(in_2), .out_3(out_3[6]));
  _1_bit_MEM u_1_bit_mem_8 (.S(in_1[7]), .E(in_2), .out_3(out_3[7]));
endmodule

module Enable_8 (
  input  [7:0] in_1,
  input  in_2,
  output [7:0] out_3
);

  wire and_1_out, and_2_out, and_3_out, and_4_out, and_5_out, and_6_out, and_7_out, and_8_out;

  and and_1 (and_1_out, in_1[0], in_2);
  and and_2 (and_2_out, in_1[1], in_2);
  and and_3 (and_3_out, in_1[2], in_2);
  and and_4 (and_4_out, in_1[3], in_2);
  and and_5 (and_5_out, in_1[4], in_2);
  and and_6 (and_6_out, in_1[5], in_2);
  and and_7 (and_7_out, in_1[6], in_2);
  and and_8 (and_8_out, in_1[7], in_2);
  assign out_3[0] = in_2 ? and_1_out : 1'bz;  // Controlled_Buffer controlled_buffer_1
  assign out_3[1] = in_2 ? and_2_out : 1'bz;  // Controlled_Buffer controlled_buffer_2
  assign out_3[2] = in_2 ? and_3_out : 1'bz;  // Controlled_Buffer controlled_buffer_3
  assign out_3[3] = in_2 ? and_4_out : 1'bz;  // Controlled_Buffer controlled_buffer_4
  assign out_3[4] = in_2 ? and_5_out : 1'bz;  // Controlled_Buffer controlled_buffer_5
  assign out_3[5] = in_2 ? and_6_out : 1'bz;  // Controlled_Buffer controlled_buffer_6
  assign out_3[6] = in_2 ? and_7_out : 1'bz;  // Controlled_Buffer controlled_buffer_7
  assign out_3[7] = in_2 ? and_8_out : 1'bz;  // Controlled_Buffer controlled_buffer_8
endmodule

module Register (
  input  [7:0] in_1,
  input  S,
  input  E,
  output [7:0] out_4,
  output [7:0] out_5
);

  wire [7:0] enable_8_1_out_3;

  _8_bit_MEM u_8_bit_mem_1 (.in_1(in_1), .out_3(out_4), .in_2(S));
  Enable_8 enable_8_1 (.in_1(out_4), .out_3(enable_8_1_out_3), .in_2(E));
  assign out_5 = E ? enable_8_1_out_3 : 8'bz;  // Controlled_Buffer controlled_buffer_1

  // Notes on the sheet:
  //   I
endmodule

module REG_Byte (
  input  [7:0] in_1,
  input  RESET,
  input  H,
  input  V,
  input  W,
  input  R,
  output [7:0] out_7,
  output [7:0] out_8
);

  wire and_1_out, and_2_out, and_3_out, or_1_out;
  wire [7:0] register_1_out_5;

  and and_1 (and_1_out, H, V);
  and and_2 (and_2_out, and_1_out, W);
  and and_3 (and_3_out, and_1_out, R);
  or or_1 (or_1_out, RESET, and_2_out);
  assign out_7 = and_3_out ? register_1_out_5 : 8'bz;  // Controlled_Buffer controlled_buffer_1
  Register register_1 (.in_1(in_1), .out_5(register_1_out_5), .S(or_1_out), .E(and_3_out), .out_4(out_8));
endmodule

module _4_16_Decoder (
  input  [3:0] in_1,
  output out_2,
  output out_3,
  output out_4,
  output out_5,
  output out_6,
  output out_7,
  output out_8,
  output out_9,
  output out_10,
  output out_11,
  output out_12,
  output out_13,
  output out_14,
  output out_15,
  output out_16,
  output out_17
);

  wire not_1_out, not_2_out, not_3_out, not_4_out;

  not not_1 (not_1_out, in_1[0]);
  not not_2 (not_2_out, in_1[1]);
  not not_3 (not_3_out, in_1[2]);
  not not_4 (not_4_out, in_1[3]);
  and and_1 (out_2, not_4_out, not_3_out, not_2_out, not_1_out);
  and and_2 (out_3, in_1[3], not_3_out, not_2_out, not_1_out);
  and and_3 (out_4, not_4_out, in_1[2], not_2_out, not_1_out);
  and and_4 (out_5, in_1[3], in_1[2], not_2_out, not_1_out);
  and and_5 (out_6, not_4_out, not_3_out, in_1[1], not_1_out);
  and and_6 (out_7, in_1[3], not_3_out, in_1[1], not_1_out);
  and and_7 (out_8, not_4_out, in_1[2], in_1[1], not_1_out);
  and and_8 (out_9, in_1[3], in_1[2], in_1[1], not_1_out);
  and and_9 (out_10, not_4_out, not_3_out, not_2_out, in_1[0]);
  and and_10 (out_11, in_1[3], not_3_out, not_2_out, in_1[0]);
  and and_11 (out_12, not_4_out, in_1[2], not_2_out, in_1[0]);
  and and_12 (out_13, in_1[3], in_1[2], not_2_out, in_1[0]);
  and and_13 (out_14, not_4_out, not_3_out, in_1[1], in_1[0]);
  and and_14 (out_15, in_1[3], not_3_out, in_1[1], in_1[0]);
  and and_15 (out_16, not_4_out, in_1[2], in_1[1], in_1[0]);
  and and_16 (out_17, in_1[3], in_1[2], in_1[1], in_1[0]);
endmodule

module Half_Adder (
  input  A,
  input  B,
  output SUM,
  output Carry
);

  xor xor_1 (SUM, A, B);
  and and_1 (Carry, A, B);
endmodule

module Full_Adder (
  input  A,
  input  B,
  input  Ci,
  output SUM,
  output Co
);

  wire and_1_out, and_2_out, xor_1_out;

  xor xor_1 (xor_1_out, A, B);
  and and_1 (and_1_out, Ci, xor_1_out);
  and and_2 (and_2_out, A, B);
  xor xor_2 (SUM, xor_1_out, Ci);
  and and_3 (Co, and_1_out, and_2_out);
endmodule

module _8_bit_adder (
  input  [7:0] A,
  input  [7:0] B,
  input  Carry_in,
  output Carry_out,
  output [7:0] out_5
);

  wire full_adder_2_co, full_adder_3_co, full_adder_4_co, full_adder_5_co, full_adder_6_co, full_adder_7_co,
       full_adder_8_co;

  Full_Adder full_adder_1 (.A(A[7]), .B(B[7]), .Ci(full_adder_2_co), .SUM(out_5[7]), .Co(Carry_out));
  Full_Adder full_adder_2 (.A(A[6]), .B(B[6]), .Ci(full_adder_3_co), .SUM(out_5[6]), .Co(full_adder_2_co));
  Full_Adder full_adder_3 (.A(A[5]), .B(B[5]), .Ci(full_adder_4_co), .SUM(out_5[5]), .Co(full_adder_3_co));
  Full_Adder full_adder_4 (.A(A[4]), .B(B[4]), .Ci(full_adder_5_co), .SUM(out_5[4]), .Co(full_adder_4_co));
  Full_Adder full_adder_5 (.A(A[3]), .B(B[3]), .Ci(full_adder_6_co), .SUM(out_5[3]), .Co(full_adder_5_co));
  Full_Adder full_adder_6 (.A(A[2]), .B(B[2]), .Ci(full_adder_7_co), .SUM(out_5[2]), .Co(full_adder_6_co));
  Full_Adder full_adder_7 (.A(A[1]), .B(B[1]), .Ci(full_adder_8_co), .SUM(out_5[1]), .Co(full_adder_7_co));
  Full_Adder full_adder_8 (.A(A[0]), .B(B[0]), .Ci(Carry_in), .SUM(out_5[0]), .Co(full_adder_8_co));
endmodule

module _256_byte_RAM (
  input  Reset,
  input  R,
  input  W,
  input  [7:0] Address,
  input  [7:0] in_5,
  output [7:0] out_6
);

  wire n4_16_decoder_1_out_2, n4_16_decoder_1_out_3, n4_16_decoder_1_out_4, n4_16_decoder_1_out_5,
       n4_16_decoder_1_out_6, n4_16_decoder_1_out_7, n4_16_decoder_1_out_8, n4_16_decoder_1_out_9,
       n4_16_decoder_1_out_10, n4_16_decoder_1_out_11, n4_16_decoder_1_out_12, n4_16_decoder_1_out_13,
       n4_16_decoder_1_out_14, n4_16_decoder_1_out_15, n4_16_decoder_1_out_16, n4_16_decoder_1_out_17,
       n4_16_decoder_2_out_2, n4_16_decoder_2_out_3, n4_16_decoder_2_out_4, n4_16_decoder_2_out_5,
       n4_16_decoder_2_out_6, n4_16_decoder_2_out_7, n4_16_decoder_2_out_8, n4_16_decoder_2_out_9,
       n4_16_decoder_2_out_10, n4_16_decoder_2_out_11, n4_16_decoder_2_out_12, n4_16_decoder_2_out_13,
       n4_16_decoder_2_out_14, n4_16_decoder_2_out_15, n4_16_decoder_2_out_16, n4_16_decoder_2_out_17;
  wire [7:0] n8_bit_mem_1_out_3;

  _8_bit_MEM u_8_bit_mem_1 (.in_1(Address), .out_3(n8_bit_mem_1_out_3), .in_2(1'b1));
  _4_16_Decoder u_4_16_decoder_1 (
    .in_1(n8_bit_mem_1_out_3[7:4]), .out_2(n4_16_decoder_1_out_2), .out_3(n4_16_decoder_1_out_3),
    .out_4(n4_16_decoder_1_out_4), .out_5(n4_16_decoder_1_out_5), .out_6(n4_16_decoder_1_out_6),
    .out_7(n4_16_decoder_1_out_7), .out_8(n4_16_decoder_1_out_8), .out_9(n4_16_decoder_1_out_9),
    .out_10(n4_16_decoder_1_out_10), .out_11(n4_16_decoder_1_out_11), .out_12(n4_16_decoder_1_out_12),
    .out_13(n4_16_decoder_1_out_13), .out_14(n4_16_decoder_1_out_14), .out_15(n4_16_decoder_1_out_15),
    .out_16(n4_16_decoder_1_out_16), .out_17(n4_16_decoder_1_out_17));
  assign out_6 = R ? out_6 : 8'bz;  // Controlled_Buffer controlled_buffer_1
  REG_Byte reg_byte_1 (
    .RESET(Reset), .H(n4_16_decoder_1_out_2), .V(n4_16_decoder_2_out_17), .in_1(in_5), .out_7(out_6), .W(W),
    .R(R));  // open: out_8
  REG_Byte reg_byte_2 (
    .RESET(Reset), .H(n4_16_decoder_1_out_3), .V(n4_16_decoder_2_out_17), .in_1(in_5), .out_7(out_6), .W(W),
    .R(R));  // open: out_8
  REG_Byte reg_byte_3 (
    .RESET(Reset), .H(n4_16_decoder_1_out_4), .V(n4_16_decoder_2_out_17), .in_1(in_5), .out_7(out_6), .W(W),
    .R(R));  // open: out_8
  REG_Byte reg_byte_4 (
    .RESET(Reset), .H(n4_16_decoder_1_out_5), .V(n4_16_decoder_2_out_17), .in_1(in_5), .out_7(out_6), .W(W),
    .R(R));  // open: out_8
  REG_Byte reg_byte_5 (
    .RESET(Reset), .H(n4_16_decoder_1_out_6), .V(n4_16_decoder_2_out_17), .in_1(in_5), .out_7(out_6), .W(W),
    .R(R));  // open: out_8
  REG_Byte reg_byte_6 (
    .RESET(Reset), .H(n4_16_decoder_1_out_7), .V(n4_16_decoder_2_out_17), .in_1(in_5), .out_7(out_6), .W(W),
    .R(R));  // open: out_8
  REG_Byte reg_byte_7 (
    .RESET(Reset), .H(n4_16_decoder_1_out_8), .V(n4_16_decoder_2_out_17), .in_1(in_5), .out_7(out_6), .W(W),
    .R(R));  // open: out_8
  REG_Byte reg_byte_8 (
    .RESET(Reset), .H(n4_16_decoder_1_out_9), .V(n4_16_decoder_2_out_17), .in_1(in_5), .out_7(out_6), .W(W),
    .R(R));  // open: out_8
  REG_Byte reg_byte_9 (
    .RESET(Reset), .H(n4_16_decoder_1_out_10), .V(n4_16_decoder_2_out_17), .in_1(in_5), .out_7(out_6), .W(W),
    .R(R));  // open: out_8
  REG_Byte reg_byte_10 (
    .RESET(Reset), .H(n4_16_decoder_1_out_11), .V(n4_16_decoder_2_out_17), .in_1(in_5), .out_7(out_6), .W(W),
    .R(R));  // open: out_8
  REG_Byte reg_byte_11 (
    .RESET(Reset), .H(n4_16_decoder_1_out_12), .V(n4_16_decoder_2_out_17), .in_1(in_5), .out_7(out_6), .W(W),
    .R(R));  // open: out_8
  REG_Byte reg_byte_12 (
    .RESET(Reset), .H(n4_16_decoder_1_out_13), .V(n4_16_decoder_2_out_17), .in_1(in_5), .out_7(out_6), .W(W),
    .R(R));  // open: out_8
  REG_Byte reg_byte_13 (
    .RESET(Reset), .H(n4_16_decoder_1_out_14), .V(n4_16_decoder_2_out_17), .in_1(in_5), .out_7(out_6), .W(W),
    .R(R));  // open: out_8
  REG_Byte reg_byte_14 (
    .RESET(Reset), .H(n4_16_decoder_1_out_15), .V(n4_16_decoder_2_out_17), .in_1(in_5), .out_7(out_6), .W(W),
    .R(R));  // open: out_8
  REG_Byte reg_byte_15 (
    .RESET(Reset), .H(n4_16_decoder_1_out_16), .V(n4_16_decoder_2_out_17), .in_1(in_5), .out_7(out_6), .W(W),
    .R(R));  // open: out_8
  REG_Byte reg_byte_16 (
    .RESET(Reset), .H(n4_16_decoder_1_out_17), .V(n4_16_decoder_2_out_17), .in_1(in_5), .out_7(out_6), .W(W),
    .R(R));  // open: out_8
  REG_Byte reg_byte_17 (
    .RESET(Reset), .H(n4_16_decoder_1_out_2), .V(n4_16_decoder_2_out_16), .in_1(in_5), .out_7(out_6), .W(W),
    .R(R));  // open: out_8
  REG_Byte reg_byte_18 (
    .RESET(Reset), .H(n4_16_decoder_1_out_3), .V(n4_16_decoder_2_out_16), .in_1(in_5), .out_7(out_6), .W(W),
    .R(R));  // open: out_8
  REG_Byte reg_byte_19 (
    .RESET(Reset), .H(n4_16_decoder_1_out_4), .V(n4_16_decoder_2_out_16), .in_1(in_5), .out_7(out_6), .W(W),
    .R(R));  // open: out_8
  REG_Byte reg_byte_20 (
    .RESET(Reset), .H(n4_16_decoder_1_out_5), .V(n4_16_decoder_2_out_16), .in_1(in_5), .out_7(out_6), .W(W),
    .R(R));  // open: out_8
  REG_Byte reg_byte_21 (
    .RESET(Reset), .H(n4_16_decoder_1_out_6), .V(n4_16_decoder_2_out_16), .in_1(in_5), .out_7(out_6), .W(W),
    .R(R));  // open: out_8
  REG_Byte reg_byte_22 (
    .RESET(Reset), .H(n4_16_decoder_1_out_7), .V(n4_16_decoder_2_out_16), .in_1(in_5), .out_7(out_6), .W(W),
    .R(R));  // open: out_8
  REG_Byte reg_byte_23 (
    .RESET(Reset), .H(n4_16_decoder_1_out_8), .V(n4_16_decoder_2_out_16), .in_1(in_5), .out_7(out_6), .W(W),
    .R(R));  // open: out_8
  REG_Byte reg_byte_24 (
    .RESET(Reset), .H(n4_16_decoder_1_out_9), .V(n4_16_decoder_2_out_16), .in_1(in_5), .out_7(out_6), .W(W),
    .R(R));  // open: out_8
  REG_Byte reg_byte_25 (
    .RESET(Reset), .H(n4_16_decoder_1_out_10), .V(n4_16_decoder_2_out_16), .in_1(in_5), .out_7(out_6), .W(W),
    .R(R));  // open: out_8
  REG_Byte reg_byte_26 (
    .RESET(Reset), .H(n4_16_decoder_1_out_11), .V(n4_16_decoder_2_out_16), .in_1(in_5), .out_7(out_6), .W(W),
    .R(R));  // open: out_8
  REG_Byte reg_byte_27 (
    .RESET(Reset), .H(n4_16_decoder_1_out_12), .V(n4_16_decoder_2_out_16), .in_1(in_5), .out_7(out_6), .W(W),
    .R(R));  // open: out_8
  REG_Byte reg_byte_28 (
    .RESET(Reset), .H(n4_16_decoder_1_out_13), .V(n4_16_decoder_2_out_16), .in_1(in_5), .out_7(out_6), .W(W),
    .R(R));  // open: out_8
  REG_Byte reg_byte_29 (
    .RESET(Reset), .H(n4_16_decoder_1_out_14), .in_1(in_5), .out_7(out_6), .W(W), .R(R));  // open: out_8, V
  REG_Byte reg_byte_30 (
    .RESET(Reset), .H(n4_16_decoder_1_out_15), .V(n4_16_decoder_2_out_16), .in_1(in_5), .out_7(out_6), .W(W),
    .R(R));  // open: out_8
  REG_Byte reg_byte_31 (
    .RESET(Reset), .H(n4_16_decoder_1_out_16), .V(n4_16_decoder_2_out_16), .in_1(in_5), .out_7(out_6), .W(W),
    .R(R));  // open: out_8
  REG_Byte reg_byte_32 (
    .RESET(Reset), .H(n4_16_decoder_1_out_17), .V(n4_16_decoder_2_out_16), .in_1(in_5), .out_7(out_6), .W(W),
    .R(R));  // open: out_8
  REG_Byte reg_byte_33 (
    .RESET(Reset), .H(n4_16_decoder_1_out_2), .V(n4_16_decoder_2_out_15), .in_1(in_5), .out_7(out_6), .W(W),
    .R(R));  // open: out_8
  REG_Byte reg_byte_34 (
    .RESET(Reset), .H(n4_16_decoder_1_out_3), .V(n4_16_decoder_2_out_15), .in_1(in_5), .out_7(out_6), .W(W),
    .R(R));  // open: out_8
  REG_Byte reg_byte_35 (
    .RESET(Reset), .H(n4_16_decoder_1_out_4), .V(n4_16_decoder_2_out_15), .in_1(in_5), .out_7(out_6), .W(W),
    .R(R));  // open: out_8
  REG_Byte reg_byte_36 (
    .RESET(Reset), .H(n4_16_decoder_1_out_5), .V(n4_16_decoder_2_out_15), .in_1(in_5), .out_7(out_6), .W(W),
    .R(R));  // open: out_8
  REG_Byte reg_byte_37 (
    .RESET(Reset), .H(n4_16_decoder_1_out_6), .V(n4_16_decoder_2_out_15), .in_1(in_5), .out_7(out_6), .W(W),
    .R(R));  // open: out_8
  REG_Byte reg_byte_38 (
    .RESET(Reset), .H(n4_16_decoder_1_out_7), .V(n4_16_decoder_2_out_15), .in_1(in_5), .out_7(out_6), .W(W),
    .R(R));  // open: out_8
  REG_Byte reg_byte_39 (
    .RESET(Reset), .H(n4_16_decoder_1_out_8), .V(n4_16_decoder_2_out_15), .in_1(in_5), .out_7(out_6), .W(W),
    .R(R));  // open: out_8
  REG_Byte reg_byte_40 (
    .RESET(Reset), .H(n4_16_decoder_1_out_9), .V(n4_16_decoder_2_out_15), .in_1(in_5), .out_7(out_6), .W(W),
    .R(R));  // open: out_8
  REG_Byte reg_byte_41 (
    .RESET(Reset), .H(n4_16_decoder_1_out_10), .V(n4_16_decoder_2_out_15), .in_1(in_5), .out_7(out_6), .W(W),
    .R(R));  // open: out_8
  REG_Byte reg_byte_42 (
    .RESET(Reset), .H(n4_16_decoder_1_out_11), .V(n4_16_decoder_2_out_15), .in_1(in_5), .out_7(out_6), .W(W),
    .R(R));  // open: out_8
  REG_Byte reg_byte_43 (
    .RESET(Reset), .H(n4_16_decoder_1_out_12), .V(n4_16_decoder_2_out_15), .in_1(in_5), .out_7(out_6), .W(W),
    .R(R));  // open: out_8
  REG_Byte reg_byte_44 (
    .RESET(Reset), .H(n4_16_decoder_1_out_13), .V(n4_16_decoder_2_out_15), .in_1(in_5), .out_7(out_6), .W(W),
    .R(R));  // open: out_8
  REG_Byte reg_byte_45 (
    .RESET(Reset), .H(n4_16_decoder_1_out_14), .V(n4_16_decoder_2_out_15), .in_1(in_5), .out_7(out_6), .W(W),
    .R(R));  // open: out_8
  REG_Byte reg_byte_46 (
    .RESET(Reset), .H(n4_16_decoder_1_out_15), .V(n4_16_decoder_2_out_15), .in_1(in_5), .out_7(out_6), .W(W),
    .R(R));  // open: out_8
  REG_Byte reg_byte_47 (
    .RESET(Reset), .H(n4_16_decoder_1_out_16), .V(n4_16_decoder_2_out_15), .in_1(in_5), .out_7(out_6), .W(W),
    .R(R));  // open: out_8
  REG_Byte reg_byte_48 (
    .RESET(Reset), .H(n4_16_decoder_1_out_17), .V(n4_16_decoder_2_out_15), .in_1(in_5), .out_7(out_6), .W(W),
    .R(R));  // open: out_8
  REG_Byte reg_byte_49 (
    .RESET(Reset), .H(n4_16_decoder_1_out_2), .V(n4_16_decoder_2_out_14), .in_1(in_5), .out_7(out_6), .W(W),
    .R(R));  // open: out_8
  REG_Byte reg_byte_50 (
    .RESET(Reset), .H(n4_16_decoder_1_out_3), .V(n4_16_decoder_2_out_14), .in_1(in_5), .out_7(out_6), .W(W),
    .R(R));  // open: out_8
  REG_Byte reg_byte_51 (
    .RESET(Reset), .H(n4_16_decoder_1_out_4), .V(n4_16_decoder_2_out_14), .in_1(in_5), .out_7(out_6), .W(W),
    .R(R));  // open: out_8
  REG_Byte reg_byte_52 (
    .RESET(Reset), .H(n4_16_decoder_1_out_5), .V(n4_16_decoder_2_out_14), .in_1(in_5), .out_7(out_6), .W(W),
    .R(R));  // open: out_8
  REG_Byte reg_byte_53 (
    .RESET(Reset), .H(n4_16_decoder_1_out_6), .V(n4_16_decoder_2_out_14), .in_1(in_5), .out_7(out_6), .W(W),
    .R(R));  // open: out_8
  REG_Byte reg_byte_54 (
    .RESET(Reset), .H(n4_16_decoder_1_out_7), .V(n4_16_decoder_2_out_14), .in_1(in_5), .out_7(out_6), .W(W),
    .R(R));  // open: out_8
  REG_Byte reg_byte_55 (
    .RESET(Reset), .H(n4_16_decoder_1_out_8), .V(n4_16_decoder_2_out_14), .in_1(in_5), .out_7(out_6), .W(W),
    .R(R));  // open: out_8
  REG_Byte reg_byte_56 (
    .RESET(Reset), .H(n4_16_decoder_1_out_9), .V(n4_16_decoder_2_out_14), .in_1(in_5), .out_7(out_6), .W(W),
    .R(R));  // open: out_8
  REG_Byte reg_byte_57 (
    .H(n4_16_decoder_1_out_10), .V(n4_16_decoder_2_out_14), .in_1(in_5), .W(W), .R(R));  // open: out_8, RESET, out_7
  REG_Byte reg_byte_58 (
    .RESET(Reset), .H(n4_16_decoder_1_out_11), .V(n4_16_decoder_2_out_14), .in_1(in_5), .out_7(out_6), .W(W),
    .R(R));  // open: out_8
  REG_Byte reg_byte_59 (
    .RESET(Reset), .H(n4_16_decoder_1_out_12), .V(n4_16_decoder_2_out_14), .in_1(in_5), .out_7(out_6), .W(W),
    .R(R));  // open: out_8
  REG_Byte reg_byte_60 (
    .RESET(Reset), .H(n4_16_decoder_1_out_13), .V(n4_16_decoder_2_out_14), .in_1(in_5), .out_7(out_6), .W(W),
    .R(R));  // open: out_8
  REG_Byte reg_byte_61 (
    .RESET(Reset), .H(n4_16_decoder_1_out_14), .V(n4_16_decoder_2_out_14), .in_1(in_5), .out_7(out_6), .W(W),
    .R(R));  // open: out_8
  REG_Byte reg_byte_62 (
    .RESET(Reset), .H(n4_16_decoder_1_out_15), .V(n4_16_decoder_2_out_14), .in_1(in_5), .out_7(out_6), .W(W),
    .R(R));  // open: out_8
  REG_Byte reg_byte_63 (
    .RESET(Reset), .H(n4_16_decoder_1_out_16), .V(n4_16_decoder_2_out_14), .in_1(in_5), .out_7(out_6), .W(W),
    .R(R));  // open: out_8
  REG_Byte reg_byte_64 (
    .RESET(Reset), .H(n4_16_decoder_1_out_17), .V(n4_16_decoder_2_out_14), .in_1(in_5), .out_7(out_6), .W(W),
    .R(R));  // open: out_8
  REG_Byte reg_byte_65 (
    .RESET(Reset), .H(n4_16_decoder_1_out_2), .V(n4_16_decoder_2_out_13), .in_1(in_5), .out_7(out_6), .W(W),
    .R(R));  // open: out_8
  REG_Byte reg_byte_66 (
    .RESET(Reset), .H(n4_16_decoder_1_out_3), .V(n4_16_decoder_2_out_13), .in_1(in_5), .out_7(out_6), .W(W),
    .R(R));  // open: out_8
  REG_Byte reg_byte_67 (
    .RESET(Reset), .H(n4_16_decoder_1_out_4), .V(n4_16_decoder_2_out_13), .in_1(in_5), .out_7(out_6), .W(W),
    .R(R));  // open: out_8
  REG_Byte reg_byte_68 (
    .RESET(Reset), .H(n4_16_decoder_1_out_5), .V(n4_16_decoder_2_out_13), .in_1(in_5), .out_7(out_6), .W(W),
    .R(R));  // open: out_8
  REG_Byte reg_byte_69 (
    .RESET(Reset), .H(n4_16_decoder_1_out_6), .V(n4_16_decoder_2_out_13), .in_1(in_5), .out_7(out_6), .W(W),
    .R(R));  // open: out_8
  REG_Byte reg_byte_70 (
    .RESET(Reset), .H(n4_16_decoder_1_out_7), .V(n4_16_decoder_2_out_13), .in_1(in_5), .out_7(out_6), .W(W),
    .R(R));  // open: out_8
  REG_Byte reg_byte_71 (
    .RESET(Reset), .H(n4_16_decoder_1_out_8), .V(n4_16_decoder_2_out_13), .in_1(in_5), .out_7(out_6), .W(W),
    .R(R));  // open: out_8
  REG_Byte reg_byte_72 (
    .RESET(Reset), .H(n4_16_decoder_1_out_9), .V(n4_16_decoder_2_out_13), .in_1(in_5), .out_7(out_6), .W(W),
    .R(R));  // open: out_8
  REG_Byte reg_byte_73 (
    .RESET(Reset), .H(n4_16_decoder_1_out_10), .V(n4_16_decoder_2_out_13), .in_1(in_5), .out_7(out_6), .W(W),
    .R(R));  // open: out_8
  REG_Byte reg_byte_74 (
    .RESET(Reset), .H(n4_16_decoder_1_out_11), .V(n4_16_decoder_2_out_13), .in_1(in_5), .out_7(out_6), .W(W),
    .R(R));  // open: out_8
  REG_Byte reg_byte_75 (
    .RESET(Reset), .H(n4_16_decoder_1_out_12), .V(n4_16_decoder_2_out_13), .in_1(in_5), .out_7(out_6), .W(W),
    .R(R));  // open: out_8
  REG_Byte reg_byte_76 (
    .RESET(Reset), .H(n4_16_decoder_1_out_13), .V(n4_16_decoder_2_out_13), .in_1(in_5), .out_7(out_6), .W(W),
    .R(R));  // open: out_8
  REG_Byte reg_byte_77 (
    .RESET(Reset), .H(n4_16_decoder_1_out_14), .V(n4_16_decoder_2_out_13), .in_1(in_5), .out_7(out_6), .W(W),
    .R(R));  // open: out_8
  REG_Byte reg_byte_78 (
    .RESET(Reset), .H(n4_16_decoder_1_out_15), .V(n4_16_decoder_2_out_13), .in_1(in_5), .out_7(out_6), .W(W),
    .R(R));  // open: out_8
  REG_Byte reg_byte_79 (
    .RESET(Reset), .H(n4_16_decoder_1_out_16), .V(n4_16_decoder_2_out_13), .in_1(in_5), .out_7(out_6), .W(W),
    .R(R));  // open: out_8
  REG_Byte reg_byte_80 (
    .RESET(Reset), .H(n4_16_decoder_1_out_17), .V(n4_16_decoder_2_out_13), .in_1(in_5), .out_7(out_6), .W(W),
    .R(R));  // open: out_8
  REG_Byte reg_byte_81 (
    .RESET(Reset), .H(n4_16_decoder_1_out_2), .V(n4_16_decoder_2_out_12), .in_1(in_5), .out_7(out_6), .W(W),
    .R(R));  // open: out_8
  REG_Byte reg_byte_82 (
    .RESET(Reset), .H(n4_16_decoder_1_out_3), .V(n4_16_decoder_2_out_12), .in_1(in_5), .out_7(out_6), .W(W),
    .R(R));  // open: out_8
  REG_Byte reg_byte_83 (
    .RESET(Reset), .H(n4_16_decoder_1_out_4), .V(n4_16_decoder_2_out_12), .in_1(in_5), .out_7(out_6), .W(W),
    .R(R));  // open: out_8
  REG_Byte reg_byte_84 (
    .RESET(Reset), .H(n4_16_decoder_1_out_5), .V(n4_16_decoder_2_out_12), .in_1(in_5), .out_7(out_6), .W(W),
    .R(R));  // open: out_8
  REG_Byte reg_byte_85 (
    .RESET(Reset), .H(n4_16_decoder_1_out_6), .V(n4_16_decoder_2_out_12), .in_1(in_5), .out_7(out_6), .W(W),
    .R(R));  // open: out_8
  REG_Byte reg_byte_86 (
    .RESET(Reset), .H(n4_16_decoder_1_out_7), .V(n4_16_decoder_2_out_12), .in_1(in_5), .out_7(out_6), .W(W),
    .R(R));  // open: out_8
  REG_Byte reg_byte_87 (
    .RESET(Reset), .H(n4_16_decoder_1_out_8), .V(n4_16_decoder_2_out_12), .in_1(in_5), .out_7(out_6), .W(W),
    .R(R));  // open: out_8
  REG_Byte reg_byte_88 (
    .RESET(Reset), .H(n4_16_decoder_1_out_9), .V(n4_16_decoder_2_out_12), .in_1(in_5), .out_7(out_6), .W(W),
    .R(R));  // open: out_8
  REG_Byte reg_byte_89 (
    .RESET(Reset), .H(n4_16_decoder_1_out_10), .V(n4_16_decoder_2_out_12), .in_1(in_5), .out_7(out_6), .W(W),
    .R(R));  // open: out_8
  REG_Byte reg_byte_90 (
    .RESET(Reset), .H(n4_16_decoder_1_out_11), .V(n4_16_decoder_2_out_12), .in_1(in_5), .out_7(out_6), .W(W),
    .R(R));  // open: out_8
  REG_Byte reg_byte_91 (
    .RESET(Reset), .H(n4_16_decoder_1_out_12), .V(n4_16_decoder_2_out_12), .in_1(in_5), .out_7(out_6), .W(W),
    .R(R));  // open: out_8
  REG_Byte reg_byte_92 (
    .RESET(Reset), .H(n4_16_decoder_1_out_13), .V(n4_16_decoder_2_out_12), .in_1(in_5), .out_7(out_6), .W(W),
    .R(R));  // open: out_8
  REG_Byte reg_byte_93 (
    .RESET(Reset), .H(n4_16_decoder_1_out_14), .V(n4_16_decoder_2_out_12), .in_1(in_5), .out_7(out_6), .W(W),
    .R(R));  // open: out_8
  REG_Byte reg_byte_94 (
    .RESET(Reset), .H(n4_16_decoder_1_out_15), .V(n4_16_decoder_2_out_12), .in_1(in_5), .out_7(out_6), .W(W),
    .R(R));  // open: out_8
  REG_Byte reg_byte_95 (
    .RESET(Reset), .H(n4_16_decoder_1_out_16), .V(n4_16_decoder_2_out_12), .in_1(in_5), .out_7(out_6), .W(W),
    .R(R));  // open: out_8
  REG_Byte reg_byte_96 (
    .RESET(Reset), .H(n4_16_decoder_1_out_17), .V(n4_16_decoder_2_out_12), .in_1(in_5), .out_7(out_6), .W(W),
    .R(R));  // open: out_8
  _4_16_Decoder u_4_16_decoder_2 (
    .in_1(n8_bit_mem_1_out_3[3:0]), .out_2(n4_16_decoder_2_out_2), .out_3(n4_16_decoder_2_out_3),
    .out_4(n4_16_decoder_2_out_4), .out_5(n4_16_decoder_2_out_5), .out_6(n4_16_decoder_2_out_6),
    .out_7(n4_16_decoder_2_out_7), .out_8(n4_16_decoder_2_out_8), .out_9(n4_16_decoder_2_out_9),
    .out_10(n4_16_decoder_2_out_10), .out_11(n4_16_decoder_2_out_11), .out_12(n4_16_decoder_2_out_12),
    .out_13(n4_16_decoder_2_out_13), .out_14(n4_16_decoder_2_out_14), .out_15(n4_16_decoder_2_out_15),
    .out_16(n4_16_decoder_2_out_16), .out_17(n4_16_decoder_2_out_17));
  REG_Byte reg_byte_97 (
    .RESET(Reset), .H(n4_16_decoder_1_out_2), .V(n4_16_decoder_2_out_11), .in_1(in_5), .out_7(out_6), .W(W),
    .R(R));  // open: out_8
  REG_Byte reg_byte_98 (
    .RESET(Reset), .H(n4_16_decoder_1_out_3), .V(n4_16_decoder_2_out_11), .in_1(in_5), .out_7(out_6), .W(W),
    .R(R));  // open: out_8
  REG_Byte reg_byte_99 (
    .RESET(Reset), .H(n4_16_decoder_1_out_4), .V(n4_16_decoder_2_out_11), .in_1(in_5), .out_7(out_6), .W(W),
    .R(R));  // open: out_8
  REG_Byte reg_byte_100 (
    .RESET(Reset), .H(n4_16_decoder_1_out_5), .V(n4_16_decoder_2_out_11), .in_1(in_5), .out_7(out_6), .W(W),
    .R(R));  // open: out_8
  REG_Byte reg_byte_101 (
    .RESET(Reset), .H(n4_16_decoder_1_out_6), .V(n4_16_decoder_2_out_11), .in_1(in_5), .out_7(out_6), .W(W),
    .R(R));  // open: out_8
  REG_Byte reg_byte_102 (
    .RESET(Reset), .H(n4_16_decoder_1_out_7), .V(n4_16_decoder_2_out_11), .in_1(in_5), .out_7(out_6), .W(W),
    .R(R));  // open: out_8
  REG_Byte reg_byte_103 (
    .RESET(Reset), .H(n4_16_decoder_1_out_8), .V(n4_16_decoder_2_out_11), .in_1(in_5), .out_7(out_6), .W(W),
    .R(R));  // open: out_8
  REG_Byte reg_byte_104 (
    .RESET(Reset), .H(n4_16_decoder_1_out_9), .V(n4_16_decoder_2_out_11), .in_1(in_5), .out_7(out_6), .W(W),
    .R(R));  // open: out_8
  REG_Byte reg_byte_105 (
    .RESET(Reset), .H(n4_16_decoder_1_out_10), .V(n4_16_decoder_2_out_11), .in_1(in_5), .out_7(out_6), .W(W),
    .R(R));  // open: out_8
  REG_Byte reg_byte_106 (
    .RESET(Reset), .H(n4_16_decoder_1_out_11), .V(n4_16_decoder_2_out_11), .in_1(in_5), .out_7(out_6), .W(W),
    .R(R));  // open: out_8
  REG_Byte reg_byte_107 (
    .RESET(Reset), .H(n4_16_decoder_1_out_12), .V(n4_16_decoder_2_out_11), .in_1(in_5), .out_7(out_6), .W(W),
    .R(R));  // open: out_8
  REG_Byte reg_byte_108 (
    .RESET(Reset), .H(n4_16_decoder_1_out_13), .V(n4_16_decoder_2_out_11), .in_1(in_5), .out_7(out_6), .W(W),
    .R(R));  // open: out_8
  REG_Byte reg_byte_109 (
    .RESET(Reset), .H(n4_16_decoder_1_out_14), .V(n4_16_decoder_2_out_11), .in_1(in_5), .out_7(out_6), .W(W),
    .R(R));  // open: out_8
  REG_Byte reg_byte_110 (
    .RESET(Reset), .H(n4_16_decoder_1_out_15), .V(n4_16_decoder_2_out_11), .in_1(in_5), .out_7(out_6), .W(W),
    .R(R));  // open: out_8
  REG_Byte reg_byte_111 (
    .RESET(Reset), .H(n4_16_decoder_1_out_16), .V(n4_16_decoder_2_out_11), .in_1(in_5), .out_7(out_6), .W(W),
    .R(R));  // open: out_8
  REG_Byte reg_byte_112 (
    .RESET(Reset), .H(n4_16_decoder_1_out_17), .V(n4_16_decoder_2_out_11), .in_1(in_5), .out_7(out_6), .W(W),
    .R(R));  // open: out_8
  REG_Byte reg_byte_113 (
    .RESET(Reset), .H(n4_16_decoder_1_out_2), .V(n4_16_decoder_2_out_10), .in_1(in_5), .out_7(out_6), .W(W),
    .R(R));  // open: out_8
  REG_Byte reg_byte_114 (
    .RESET(Reset), .H(n4_16_decoder_1_out_3), .V(n4_16_decoder_2_out_10), .in_1(in_5), .out_7(out_6), .W(W),
    .R(R));  // open: out_8
  REG_Byte reg_byte_115 (
    .RESET(Reset), .H(n4_16_decoder_1_out_4), .V(n4_16_decoder_2_out_10), .in_1(in_5), .out_7(out_6), .W(W),
    .R(R));  // open: out_8
  REG_Byte reg_byte_116 (
    .RESET(Reset), .H(n4_16_decoder_1_out_5), .V(n4_16_decoder_2_out_10), .in_1(in_5), .out_7(out_6), .W(W),
    .R(R));  // open: out_8
  REG_Byte reg_byte_117 (
    .RESET(Reset), .H(n4_16_decoder_1_out_6), .V(n4_16_decoder_2_out_10), .in_1(in_5), .out_7(out_6), .W(W),
    .R(R));  // open: out_8
  REG_Byte reg_byte_118 (
    .RESET(Reset), .H(n4_16_decoder_1_out_7), .V(n4_16_decoder_2_out_10), .in_1(in_5), .out_7(out_6), .W(W),
    .R(R));  // open: out_8
  REG_Byte reg_byte_119 (
    .RESET(Reset), .H(n4_16_decoder_1_out_8), .V(n4_16_decoder_2_out_10), .in_1(in_5), .out_7(out_6), .W(W),
    .R(R));  // open: out_8
  REG_Byte reg_byte_120 (
    .RESET(Reset), .H(n4_16_decoder_1_out_9), .V(n4_16_decoder_2_out_10), .in_1(in_5), .out_7(out_6), .W(W),
    .R(R));  // open: out_8
  REG_Byte reg_byte_121 (
    .RESET(Reset), .H(n4_16_decoder_1_out_10), .V(n4_16_decoder_2_out_10), .in_1(in_5), .out_7(out_6), .W(W),
    .R(R));  // open: out_8
  REG_Byte reg_byte_122 (
    .RESET(Reset), .H(n4_16_decoder_1_out_11), .V(n4_16_decoder_2_out_10), .in_1(in_5), .out_7(out_6), .W(W),
    .R(R));  // open: out_8
  REG_Byte reg_byte_123 (
    .RESET(Reset), .H(n4_16_decoder_1_out_12), .V(n4_16_decoder_2_out_10), .in_1(in_5), .out_7(out_6), .W(W),
    .R(R));  // open: out_8
  REG_Byte reg_byte_124 (
    .RESET(Reset), .H(n4_16_decoder_1_out_13), .V(n4_16_decoder_2_out_10), .in_1(in_5), .out_7(out_6), .W(W),
    .R(R));  // open: out_8
  REG_Byte reg_byte_125 (
    .RESET(Reset), .H(n4_16_decoder_1_out_14), .V(n4_16_decoder_2_out_10), .in_1(in_5), .out_7(out_6), .W(W),
    .R(R));  // open: out_8
  REG_Byte reg_byte_126 (
    .RESET(Reset), .H(n4_16_decoder_1_out_15), .V(n4_16_decoder_2_out_10), .in_1(in_5), .out_7(out_6), .W(W),
    .R(R));  // open: out_8
  REG_Byte reg_byte_127 (
    .RESET(Reset), .H(n4_16_decoder_1_out_16), .V(n4_16_decoder_2_out_10), .in_1(in_5), .out_7(out_6), .W(W),
    .R(R));  // open: out_8
  REG_Byte reg_byte_128 (
    .RESET(Reset), .H(n4_16_decoder_1_out_17), .V(n4_16_decoder_2_out_10), .in_1(in_5), .out_7(out_6), .W(W),
    .R(R));  // open: out_8
  REG_Byte reg_byte_129 (
    .RESET(Reset), .H(n4_16_decoder_1_out_2), .V(n4_16_decoder_2_out_9), .in_1(in_5), .out_7(out_6), .W(W),
    .R(R));  // open: out_8
  REG_Byte reg_byte_130 (
    .RESET(Reset), .H(n4_16_decoder_1_out_3), .V(n4_16_decoder_2_out_9), .in_1(in_5), .out_7(out_6), .W(W),
    .R(R));  // open: out_8
  REG_Byte reg_byte_131 (
    .RESET(Reset), .H(n4_16_decoder_1_out_4), .V(n4_16_decoder_2_out_9), .in_1(in_5), .out_7(out_6), .W(W),
    .R(R));  // open: out_8
  REG_Byte reg_byte_132 (
    .RESET(Reset), .H(n4_16_decoder_1_out_5), .V(n4_16_decoder_2_out_9), .in_1(in_5), .out_7(out_6), .W(W),
    .R(R));  // open: out_8
  REG_Byte reg_byte_133 (
    .RESET(Reset), .H(n4_16_decoder_1_out_6), .V(n4_16_decoder_2_out_9), .in_1(in_5), .out_7(out_6), .W(W),
    .R(R));  // open: out_8
  REG_Byte reg_byte_134 (
    .RESET(Reset), .H(n4_16_decoder_1_out_7), .V(n4_16_decoder_2_out_9), .in_1(in_5), .out_7(out_6), .W(W),
    .R(R));  // open: out_8
  REG_Byte reg_byte_135 (
    .RESET(Reset), .H(n4_16_decoder_1_out_8), .V(n4_16_decoder_2_out_9), .in_1(in_5), .out_7(out_6), .W(W),
    .R(R));  // open: out_8
  REG_Byte reg_byte_136 (
    .RESET(Reset), .H(n4_16_decoder_1_out_9), .V(n4_16_decoder_2_out_9), .in_1(in_5), .out_7(out_6), .W(W),
    .R(R));  // open: out_8
  REG_Byte reg_byte_137 (
    .RESET(Reset), .H(n4_16_decoder_1_out_10), .V(n4_16_decoder_2_out_9), .in_1(in_5), .out_7(out_6), .W(W),
    .R(R));  // open: out_8
  REG_Byte reg_byte_138 (
    .RESET(Reset), .H(n4_16_decoder_1_out_11), .V(n4_16_decoder_2_out_9), .in_1(in_5), .out_7(out_6), .W(W),
    .R(R));  // open: out_8
  REG_Byte reg_byte_139 (
    .RESET(Reset), .H(n4_16_decoder_1_out_12), .V(n4_16_decoder_2_out_9), .in_1(in_5), .out_7(out_6), .W(W),
    .R(R));  // open: out_8
  REG_Byte reg_byte_140 (
    .RESET(Reset), .H(n4_16_decoder_1_out_13), .V(n4_16_decoder_2_out_9), .in_1(in_5), .out_7(out_6), .W(W),
    .R(R));  // open: out_8
  REG_Byte reg_byte_141 (
    .RESET(Reset), .H(n4_16_decoder_1_out_14), .V(n4_16_decoder_2_out_9), .in_1(in_5), .out_7(out_6), .W(W),
    .R(R));  // open: out_8
  REG_Byte reg_byte_142 (
    .RESET(Reset), .H(n4_16_decoder_1_out_15), .V(n4_16_decoder_2_out_9), .in_1(in_5), .out_7(out_6), .W(W),
    .R(R));  // open: out_8
  REG_Byte reg_byte_143 (
    .RESET(Reset), .H(n4_16_decoder_1_out_16), .V(n4_16_decoder_2_out_9), .in_1(in_5), .out_7(out_6), .W(W),
    .R(R));  // open: out_8
  REG_Byte reg_byte_144 (
    .RESET(Reset), .H(n4_16_decoder_1_out_17), .V(n4_16_decoder_2_out_9), .in_1(in_5), .out_7(out_6), .W(W),
    .R(R));  // open: out_8
  REG_Byte reg_byte_145 (
    .RESET(Reset), .H(n4_16_decoder_1_out_2), .V(n4_16_decoder_2_out_8), .in_1(in_5), .out_7(out_6), .W(W),
    .R(R));  // open: out_8
  REG_Byte reg_byte_146 (
    .RESET(Reset), .H(n4_16_decoder_1_out_3), .V(n4_16_decoder_2_out_8), .in_1(in_5), .out_7(out_6), .W(W),
    .R(R));  // open: out_8
  REG_Byte reg_byte_147 (
    .RESET(Reset), .H(n4_16_decoder_1_out_4), .V(n4_16_decoder_2_out_8), .in_1(in_5), .out_7(out_6), .W(W),
    .R(R));  // open: out_8
  REG_Byte reg_byte_148 (
    .RESET(Reset), .H(n4_16_decoder_1_out_5), .V(n4_16_decoder_2_out_8), .in_1(in_5), .out_7(out_6), .W(W),
    .R(R));  // open: out_8
  REG_Byte reg_byte_149 (
    .RESET(Reset), .H(n4_16_decoder_1_out_6), .V(n4_16_decoder_2_out_8), .in_1(in_5), .out_7(out_6), .W(W),
    .R(R));  // open: out_8
  REG_Byte reg_byte_150 (
    .RESET(Reset), .H(n4_16_decoder_1_out_7), .V(n4_16_decoder_2_out_8), .in_1(in_5), .out_7(out_6), .W(W),
    .R(R));  // open: out_8
  REG_Byte reg_byte_151 (
    .RESET(Reset), .H(n4_16_decoder_1_out_8), .V(n4_16_decoder_2_out_8), .in_1(in_5), .out_7(out_6), .W(W),
    .R(R));  // open: out_8
  REG_Byte reg_byte_152 (
    .RESET(Reset), .H(n4_16_decoder_1_out_9), .V(n4_16_decoder_2_out_8), .in_1(in_5), .out_7(out_6), .W(W),
    .R(R));  // open: out_8
  REG_Byte reg_byte_153 (
    .RESET(Reset), .H(n4_16_decoder_1_out_10), .V(n4_16_decoder_2_out_8), .in_1(in_5), .out_7(out_6), .W(W),
    .R(R));  // open: out_8
  REG_Byte reg_byte_154 (
    .RESET(Reset), .H(n4_16_decoder_1_out_11), .V(n4_16_decoder_2_out_8), .in_1(in_5), .out_7(out_6), .W(W),
    .R(R));  // open: out_8
  REG_Byte reg_byte_155 (
    .RESET(Reset), .H(n4_16_decoder_1_out_12), .V(n4_16_decoder_2_out_8), .in_1(in_5), .out_7(out_6), .W(W),
    .R(R));  // open: out_8
  REG_Byte reg_byte_156 (
    .RESET(Reset), .H(n4_16_decoder_1_out_13), .V(n4_16_decoder_2_out_8), .in_1(in_5), .out_7(out_6), .W(W),
    .R(R));  // open: out_8
  REG_Byte reg_byte_157 (
    .RESET(Reset), .H(n4_16_decoder_1_out_14), .V(n4_16_decoder_2_out_8), .in_1(in_5), .out_7(out_6), .W(W),
    .R(R));  // open: out_8
  REG_Byte reg_byte_158 (
    .RESET(Reset), .H(n4_16_decoder_1_out_15), .V(n4_16_decoder_2_out_8), .in_1(in_5), .out_7(out_6), .W(W),
    .R(R));  // open: out_8
  REG_Byte reg_byte_159 (
    .RESET(Reset), .H(n4_16_decoder_1_out_16), .V(n4_16_decoder_2_out_8), .in_1(in_5), .out_7(out_6), .W(W),
    .R(R));  // open: out_8
  REG_Byte reg_byte_160 (
    .RESET(Reset), .H(n4_16_decoder_1_out_17), .V(n4_16_decoder_2_out_8), .in_1(in_5), .out_7(out_6), .W(W),
    .R(R));  // open: out_8
  REG_Byte reg_byte_161 (
    .RESET(Reset), .H(n4_16_decoder_1_out_2), .V(n4_16_decoder_2_out_7), .in_1(in_5), .out_7(out_6), .W(W),
    .R(R));  // open: out_8
  REG_Byte reg_byte_162 (
    .RESET(Reset), .H(n4_16_decoder_1_out_3), .V(n4_16_decoder_2_out_7), .in_1(in_5), .out_7(out_6), .W(W),
    .R(R));  // open: out_8
  REG_Byte reg_byte_163 (
    .RESET(Reset), .H(n4_16_decoder_1_out_4), .V(n4_16_decoder_2_out_7), .in_1(in_5), .out_7(out_6), .W(W),
    .R(R));  // open: out_8
  REG_Byte reg_byte_164 (
    .RESET(Reset), .H(n4_16_decoder_1_out_5), .V(n4_16_decoder_2_out_7), .in_1(in_5), .out_7(out_6), .W(W),
    .R(R));  // open: out_8
  REG_Byte reg_byte_165 (
    .RESET(Reset), .H(n4_16_decoder_1_out_6), .V(n4_16_decoder_2_out_7), .in_1(in_5), .out_7(out_6), .W(W),
    .R(R));  // open: out_8
  REG_Byte reg_byte_166 (
    .RESET(Reset), .H(n4_16_decoder_1_out_7), .V(n4_16_decoder_2_out_7), .in_1(in_5), .out_7(out_6), .W(W),
    .R(R));  // open: out_8
  REG_Byte reg_byte_167 (
    .RESET(Reset), .H(n4_16_decoder_1_out_8), .V(n4_16_decoder_2_out_7), .in_1(in_5), .out_7(out_6), .W(W),
    .R(R));  // open: out_8
  REG_Byte reg_byte_168 (
    .RESET(Reset), .H(n4_16_decoder_1_out_9), .V(n4_16_decoder_2_out_7), .in_1(in_5), .out_7(out_6), .W(W),
    .R(R));  // open: out_8
  REG_Byte reg_byte_169 (
    .RESET(Reset), .H(n4_16_decoder_1_out_10), .V(n4_16_decoder_2_out_7), .in_1(in_5), .out_7(out_6), .W(W),
    .R(R));  // open: out_8
  REG_Byte reg_byte_170 (
    .RESET(Reset), .H(n4_16_decoder_1_out_11), .V(n4_16_decoder_2_out_7), .in_1(in_5), .out_7(out_6), .W(W),
    .R(R));  // open: out_8
  REG_Byte reg_byte_171 (
    .RESET(Reset), .H(n4_16_decoder_1_out_12), .V(n4_16_decoder_2_out_7), .in_1(in_5), .out_7(out_6), .W(W),
    .R(R));  // open: out_8
  REG_Byte reg_byte_172 (
    .RESET(Reset), .H(n4_16_decoder_1_out_13), .V(n4_16_decoder_2_out_7), .in_1(in_5), .out_7(out_6), .W(W),
    .R(R));  // open: out_8
  REG_Byte reg_byte_173 (
    .RESET(Reset), .H(n4_16_decoder_1_out_14), .V(n4_16_decoder_2_out_7), .in_1(in_5), .out_7(out_6), .W(W),
    .R(R));  // open: out_8
  REG_Byte reg_byte_174 (
    .RESET(Reset), .H(n4_16_decoder_1_out_15), .V(n4_16_decoder_2_out_7), .in_1(in_5), .out_7(out_6), .W(W),
    .R(R));  // open: out_8
  REG_Byte reg_byte_175 (
    .RESET(Reset), .H(n4_16_decoder_1_out_16), .V(n4_16_decoder_2_out_7), .in_1(in_5), .out_7(out_6), .W(W),
    .R(R));  // open: out_8
  REG_Byte reg_byte_176 (
    .RESET(Reset), .H(n4_16_decoder_1_out_17), .V(n4_16_decoder_2_out_7), .in_1(in_5), .out_7(out_6), .W(W),
    .R(R));  // open: out_8
  REG_Byte reg_byte_177 (
    .RESET(Reset), .H(n4_16_decoder_1_out_2), .V(n4_16_decoder_2_out_6), .in_1(in_5), .out_7(out_6), .W(W),
    .R(R));  // open: out_8
  REG_Byte reg_byte_178 (
    .RESET(Reset), .H(n4_16_decoder_1_out_3), .V(n4_16_decoder_2_out_6), .in_1(in_5), .out_7(out_6), .W(W),
    .R(R));  // open: out_8
  REG_Byte reg_byte_179 (
    .RESET(Reset), .H(n4_16_decoder_1_out_4), .V(n4_16_decoder_2_out_6), .in_1(in_5), .out_7(out_6), .W(W),
    .R(R));  // open: out_8
  REG_Byte reg_byte_180 (
    .RESET(Reset), .H(n4_16_decoder_1_out_5), .V(n4_16_decoder_2_out_6), .in_1(in_5), .out_7(out_6), .W(W),
    .R(R));  // open: out_8
  REG_Byte reg_byte_181 (
    .RESET(Reset), .H(n4_16_decoder_1_out_6), .V(n4_16_decoder_2_out_6), .in_1(in_5), .out_7(out_6), .W(W),
    .R(R));  // open: out_8
  REG_Byte reg_byte_182 (
    .RESET(Reset), .H(n4_16_decoder_1_out_7), .in_1(in_5), .out_7(out_6), .W(W), .R(R));  // open: out_8, V
  REG_Byte reg_byte_183 (
    .RESET(Reset), .H(n4_16_decoder_1_out_8), .V(n4_16_decoder_2_out_6), .in_1(in_5), .out_7(out_6), .W(W),
    .R(R));  // open: out_8
  REG_Byte reg_byte_184 (
    .RESET(Reset), .H(n4_16_decoder_1_out_9), .V(n4_16_decoder_2_out_6), .in_1(in_5), .out_7(out_6), .W(W),
    .R(R));  // open: out_8
  REG_Byte reg_byte_185 (
    .RESET(Reset), .H(n4_16_decoder_1_out_10), .V(n4_16_decoder_2_out_6), .in_1(in_5), .out_7(out_6), .W(W),
    .R(R));  // open: out_8
  REG_Byte reg_byte_186 (
    .RESET(Reset), .H(n4_16_decoder_1_out_11), .V(n4_16_decoder_2_out_6), .in_1(in_5), .out_7(out_6), .W(W),
    .R(R));  // open: out_8
  REG_Byte reg_byte_187 (
    .RESET(Reset), .H(n4_16_decoder_1_out_12), .V(n4_16_decoder_2_out_6), .in_1(in_5), .out_7(out_6), .W(W),
    .R(R));  // open: out_8
  REG_Byte reg_byte_188 (
    .H(n4_16_decoder_1_out_13), .V(n4_16_decoder_2_out_6), .in_1(in_5), .W(W), .R(R));  // open: out_8, RESET, out_7
  REG_Byte reg_byte_189 (
    .RESET(Reset), .H(n4_16_decoder_1_out_14), .V(n4_16_decoder_2_out_6), .in_1(in_5), .out_7(out_6), .W(W),
    .R(R));  // open: out_8
  REG_Byte reg_byte_190 (
    .RESET(Reset), .H(n4_16_decoder_1_out_15), .V(n4_16_decoder_2_out_6), .in_1(in_5), .out_7(out_6), .W(W),
    .R(R));  // open: out_8
  REG_Byte reg_byte_191 (
    .RESET(Reset), .H(n4_16_decoder_1_out_16), .V(n4_16_decoder_2_out_6), .in_1(in_5), .out_7(out_6), .W(W),
    .R(R));  // open: out_8
  REG_Byte reg_byte_192 (
    .RESET(Reset), .H(n4_16_decoder_1_out_17), .V(n4_16_decoder_2_out_6), .in_1(in_5), .out_7(out_6), .W(W),
    .R(R));  // open: out_8
  REG_Byte reg_byte_193 (
    .RESET(Reset), .H(n4_16_decoder_1_out_2), .V(n4_16_decoder_2_out_5), .in_1(in_5), .out_7(out_6), .W(W),
    .R(R));  // open: out_8
  REG_Byte reg_byte_194 (
    .RESET(Reset), .H(n4_16_decoder_1_out_3), .V(n4_16_decoder_2_out_5), .in_1(in_5), .out_7(out_6), .W(W),
    .R(R));  // open: out_8
  REG_Byte reg_byte_195 (
    .RESET(Reset), .H(n4_16_decoder_1_out_4), .V(n4_16_decoder_2_out_5), .in_1(in_5), .out_7(out_6), .W(W),
    .R(R));  // open: out_8
  REG_Byte reg_byte_196 (
    .RESET(Reset), .H(n4_16_decoder_1_out_5), .V(n4_16_decoder_2_out_5), .in_1(in_5), .out_7(out_6), .W(W),
    .R(R));  // open: out_8
  REG_Byte reg_byte_197 (
    .RESET(Reset), .H(n4_16_decoder_1_out_6), .V(n4_16_decoder_2_out_5), .in_1(in_5), .out_7(out_6), .W(W),
    .R(R));  // open: out_8
  REG_Byte reg_byte_198 (
    .RESET(Reset), .H(n4_16_decoder_1_out_7), .V(n4_16_decoder_2_out_5), .in_1(in_5), .out_7(out_6), .W(W),
    .R(R));  // open: out_8
  REG_Byte reg_byte_199 (
    .RESET(Reset), .H(n4_16_decoder_1_out_8), .V(n4_16_decoder_2_out_5), .in_1(in_5), .out_7(out_6), .W(W),
    .R(R));  // open: out_8
  REG_Byte reg_byte_200 (
    .RESET(Reset), .H(n4_16_decoder_1_out_9), .V(n4_16_decoder_2_out_5), .in_1(in_5), .out_7(out_6), .W(W),
    .R(R));  // open: out_8
  REG_Byte reg_byte_201 (
    .RESET(Reset), .H(n4_16_decoder_1_out_10), .V(n4_16_decoder_2_out_5), .in_1(in_5), .out_7(out_6), .W(W),
    .R(R));  // open: out_8
  REG_Byte reg_byte_202 (
    .RESET(Reset), .H(n4_16_decoder_1_out_11), .V(n4_16_decoder_2_out_5), .in_1(in_5), .out_7(out_6), .W(W),
    .R(R));  // open: out_8
  REG_Byte reg_byte_203 (
    .RESET(Reset), .H(n4_16_decoder_1_out_12), .in_1(in_5), .out_7(out_6), .W(W), .R(R));  // open: out_8, V
  REG_Byte reg_byte_204 (
    .RESET(Reset), .H(n4_16_decoder_1_out_13), .V(n4_16_decoder_2_out_5), .in_1(in_5), .out_7(out_6), .W(W),
    .R(R));  // open: out_8
  REG_Byte reg_byte_205 (
    .RESET(Reset), .H(n4_16_decoder_1_out_14), .V(n4_16_decoder_2_out_5), .in_1(in_5), .out_7(out_6), .W(W),
    .R(R));  // open: out_8
  REG_Byte reg_byte_206 (
    .H(n4_16_decoder_1_out_15), .V(n4_16_decoder_2_out_5), .in_1(in_5), .W(W), .R(R));  // open: out_8, RESET, out_7
  REG_Byte reg_byte_207 (
    .RESET(Reset), .H(n4_16_decoder_1_out_16), .V(n4_16_decoder_2_out_5), .in_1(in_5), .out_7(out_6), .W(W),
    .R(R));  // open: out_8
  REG_Byte reg_byte_208 (
    .RESET(Reset), .H(n4_16_decoder_1_out_17), .V(n4_16_decoder_2_out_5), .in_1(in_5), .out_7(out_6), .W(W),
    .R(R));  // open: out_8
  REG_Byte reg_byte_209 (
    .RESET(Reset), .H(n4_16_decoder_1_out_2), .V(n4_16_decoder_2_out_4), .in_1(in_5), .out_7(out_6), .W(W),
    .R(R));  // open: out_8
  REG_Byte reg_byte_210 (
    .RESET(Reset), .H(n4_16_decoder_1_out_3), .V(n4_16_decoder_2_out_4), .in_1(in_5), .out_7(out_6), .W(W),
    .R(R));  // open: out_8
  REG_Byte reg_byte_211 (
    .RESET(Reset), .H(n4_16_decoder_1_out_4), .V(n4_16_decoder_2_out_4), .in_1(in_5), .out_7(out_6), .W(W),
    .R(R));  // open: out_8
  REG_Byte reg_byte_212 (
    .RESET(Reset), .H(n4_16_decoder_1_out_5), .V(n4_16_decoder_2_out_4), .in_1(in_5), .out_7(out_6), .W(W),
    .R(R));  // open: out_8
  REG_Byte reg_byte_213 (
    .RESET(Reset), .H(n4_16_decoder_1_out_6), .V(n4_16_decoder_2_out_4), .in_1(in_5), .out_7(out_6), .W(W),
    .R(R));  // open: out_8
  REG_Byte reg_byte_214 (
    .RESET(Reset), .H(n4_16_decoder_1_out_7), .V(n4_16_decoder_2_out_4), .in_1(in_5), .out_7(out_6), .W(W),
    .R(R));  // open: out_8
  REG_Byte reg_byte_215 (
    .H(n4_16_decoder_1_out_8), .V(n4_16_decoder_2_out_4), .in_1(in_5), .W(W), .R(R));  // open: out_8, RESET, out_7
  REG_Byte reg_byte_216 (
    .RESET(Reset), .H(n4_16_decoder_1_out_9), .V(n4_16_decoder_2_out_4), .in_1(in_5), .out_7(out_6), .W(W),
    .R(R));  // open: out_8
  REG_Byte reg_byte_217 (
    .RESET(Reset), .H(n4_16_decoder_1_out_10), .V(n4_16_decoder_2_out_4), .in_1(in_5), .out_7(out_6), .W(W),
    .R(R));  // open: out_8
  REG_Byte reg_byte_218 (
    .RESET(Reset), .H(n4_16_decoder_1_out_11), .V(n4_16_decoder_2_out_4), .in_1(in_5), .out_7(out_6), .W(W),
    .R(R));  // open: out_8
  REG_Byte reg_byte_219 (
    .RESET(Reset), .H(n4_16_decoder_1_out_12), .V(n4_16_decoder_2_out_4), .in_1(in_5), .out_7(out_6), .W(W),
    .R(R));  // open: out_8
  REG_Byte reg_byte_220 (
    .RESET(Reset), .H(n4_16_decoder_1_out_13), .V(n4_16_decoder_2_out_4), .in_1(in_5), .out_7(out_6), .W(W),
    .R(R));  // open: out_8
  REG_Byte reg_byte_221 (
    .RESET(Reset), .H(n4_16_decoder_1_out_14), .V(n4_16_decoder_2_out_4), .in_1(in_5), .out_7(out_6), .W(W),
    .R(R));  // open: out_8
  REG_Byte reg_byte_222 (
    .RESET(Reset), .H(n4_16_decoder_1_out_15), .V(n4_16_decoder_2_out_4), .in_1(in_5), .out_7(out_6), .W(W),
    .R(R));  // open: out_8
  REG_Byte reg_byte_223 (
    .RESET(Reset), .H(n4_16_decoder_1_out_16), .V(n4_16_decoder_2_out_4), .in_1(in_5), .out_7(out_6), .W(W),
    .R(R));  // open: out_8
  REG_Byte reg_byte_224 (
    .RESET(Reset), .H(n4_16_decoder_1_out_17), .V(n4_16_decoder_2_out_4), .in_1(in_5), .out_7(out_6), .W(W),
    .R(R));  // open: out_8
  REG_Byte reg_byte_225 (
    .RESET(Reset), .H(n4_16_decoder_1_out_2), .V(n4_16_decoder_2_out_3), .in_1(in_5), .out_7(out_6), .W(W),
    .R(R));  // open: out_8
  REG_Byte reg_byte_226 (
    .RESET(Reset), .H(n4_16_decoder_1_out_3), .V(n4_16_decoder_2_out_3), .in_1(in_5), .out_7(out_6), .W(W),
    .R(R));  // open: out_8
  REG_Byte reg_byte_227 (
    .RESET(Reset), .H(n4_16_decoder_1_out_4), .V(n4_16_decoder_2_out_3), .in_1(in_5), .out_7(out_6), .W(W),
    .R(R));  // open: out_8
  REG_Byte reg_byte_228 (
    .RESET(Reset), .H(n4_16_decoder_1_out_5), .V(n4_16_decoder_2_out_3), .in_1(in_5), .out_7(out_6), .W(W),
    .R(R));  // open: out_8
  REG_Byte reg_byte_229 (
    .RESET(Reset), .H(n4_16_decoder_1_out_6), .V(n4_16_decoder_2_out_3), .in_1(in_5), .out_7(out_6), .W(W),
    .R(R));  // open: out_8
  REG_Byte reg_byte_230 (
    .RESET(Reset), .H(n4_16_decoder_1_out_7), .V(n4_16_decoder_2_out_3), .in_1(in_5), .out_7(out_6), .W(W),
    .R(R));  // open: out_8
  REG_Byte reg_byte_231 (
    .RESET(Reset), .H(n4_16_decoder_1_out_8), .V(n4_16_decoder_2_out_3), .in_1(in_5), .out_7(out_6), .W(W),
    .R(R));  // open: out_8
  REG_Byte reg_byte_232 (
    .RESET(Reset), .H(n4_16_decoder_1_out_9), .V(n4_16_decoder_2_out_3), .in_1(in_5), .out_7(out_6), .W(W),
    .R(R));  // open: out_8
  REG_Byte reg_byte_233 (
    .RESET(Reset), .H(n4_16_decoder_1_out_10), .V(n4_16_decoder_2_out_3), .in_1(in_5), .out_7(out_6), .W(W),
    .R(R));  // open: out_8
  REG_Byte reg_byte_234 (
    .RESET(Reset), .H(n4_16_decoder_1_out_11), .V(n4_16_decoder_2_out_3), .in_1(in_5), .out_7(out_6), .W(W),
    .R(R));  // open: out_8
  REG_Byte reg_byte_235 (
    .RESET(Reset), .H(n4_16_decoder_1_out_12), .V(n4_16_decoder_2_out_3), .in_1(in_5), .out_7(out_6), .W(W),
    .R(R));  // open: out_8
  REG_Byte reg_byte_236 (
    .RESET(Reset), .H(n4_16_decoder_1_out_13), .V(n4_16_decoder_2_out_3), .in_1(in_5), .out_7(out_6), .W(W),
    .R(R));  // open: out_8
  REG_Byte reg_byte_237 (
    .RESET(Reset), .H(n4_16_decoder_1_out_14), .V(n4_16_decoder_2_out_3), .in_1(in_5), .out_7(out_6), .W(W),
    .R(R));  // open: out_8
  REG_Byte reg_byte_238 (
    .RESET(Reset), .H(n4_16_decoder_1_out_15), .V(n4_16_decoder_2_out_3), .in_1(in_5), .out_7(out_6), .W(W),
    .R(R));  // open: out_8
  REG_Byte reg_byte_239 (
    .RESET(Reset), .H(n4_16_decoder_1_out_16), .V(n4_16_decoder_2_out_3), .in_1(in_5), .out_7(out_6), .W(W),
    .R(R));  // open: out_8
  REG_Byte reg_byte_240 (
    .RESET(Reset), .H(n4_16_decoder_1_out_17), .V(n4_16_decoder_2_out_3), .in_1(in_5), .out_7(out_6), .W(W),
    .R(R));  // open: out_8
  REG_Byte reg_byte_241 (
    .RESET(Reset), .H(n4_16_decoder_1_out_2), .V(n4_16_decoder_2_out_2), .in_1(in_5), .out_7(out_6), .W(W),
    .R(R));  // open: out_8
  REG_Byte reg_byte_242 (
    .RESET(Reset), .H(n4_16_decoder_1_out_3), .V(n4_16_decoder_2_out_2), .in_1(in_5), .out_7(out_6), .W(W),
    .R(R));  // open: out_8
  REG_Byte reg_byte_243 (
    .RESET(Reset), .H(n4_16_decoder_1_out_4), .V(n4_16_decoder_2_out_2), .in_1(in_5), .out_7(out_6), .W(W),
    .R(R));  // open: out_8
  REG_Byte reg_byte_244 (
    .RESET(Reset), .H(n4_16_decoder_1_out_5), .V(n4_16_decoder_2_out_2), .in_1(in_5), .out_7(out_6), .W(W),
    .R(R));  // open: out_8
  REG_Byte reg_byte_245 (
    .RESET(Reset), .H(n4_16_decoder_1_out_6), .V(n4_16_decoder_2_out_2), .in_1(in_5), .out_7(out_6), .W(W),
    .R(R));  // open: out_8
  REG_Byte reg_byte_246 (
    .RESET(Reset), .H(n4_16_decoder_1_out_7), .V(n4_16_decoder_2_out_2), .in_1(in_5), .out_7(out_6), .W(W),
    .R(R));  // open: out_8
  REG_Byte reg_byte_247 (
    .RESET(Reset), .H(n4_16_decoder_1_out_8), .V(n4_16_decoder_2_out_2), .in_1(in_5), .out_7(out_6), .W(W),
    .R(R));  // open: out_8
  REG_Byte reg_byte_248 (
    .RESET(Reset), .H(n4_16_decoder_1_out_9), .V(n4_16_decoder_2_out_2), .in_1(in_5), .out_7(out_6), .W(W),
    .R(R));  // open: out_8
  REG_Byte reg_byte_249 (
    .RESET(Reset), .H(n4_16_decoder_1_out_10), .V(n4_16_decoder_2_out_2), .in_1(in_5), .out_7(out_6), .W(W),
    .R(R));  // open: out_8
  REG_Byte reg_byte_250 (
    .RESET(Reset), .H(n4_16_decoder_1_out_11), .V(n4_16_decoder_2_out_2), .in_1(in_5), .out_7(out_6), .W(W),
    .R(R));  // open: out_8
  REG_Byte reg_byte_251 (
    .RESET(Reset), .H(n4_16_decoder_1_out_12), .V(n4_16_decoder_2_out_2), .in_1(in_5), .out_7(out_6), .W(W),
    .R(R));  // open: out_8
  REG_Byte reg_byte_252 (
    .RESET(Reset), .H(n4_16_decoder_1_out_13), .V(n4_16_decoder_2_out_2), .in_1(in_5), .out_7(out_6), .W(W),
    .R(R));  // open: out_8
  REG_Byte reg_byte_253 (
    .RESET(Reset), .H(n4_16_decoder_1_out_14), .V(n4_16_decoder_2_out_2), .in_1(in_5), .out_7(out_6), .W(W),
    .R(R));  // open: out_8
  REG_Byte reg_byte_254 (
    .RESET(Reset), .H(n4_16_decoder_1_out_15), .V(n4_16_decoder_2_out_2), .in_1(in_5), .out_7(out_6), .W(W),
    .R(R));  // open: out_8
  REG_Byte reg_byte_255 (
    .RESET(Reset), .H(n4_16_decoder_1_out_16), .V(n4_16_decoder_2_out_2), .in_1(in_5), .out_7(out_6), .W(W),
    .R(R));  // open: out_8
  REG_Byte reg_byte_256 (
    .RESET(Reset), .H(n4_16_decoder_1_out_17), .V(n4_16_decoder_2_out_2), .in_1(in_5), .out_7(out_6), .W(W),
    .R(R));  // open: out_8

  // Notes on the sheet:
  //   Out
  //   In
endmodule

module smallEnable (
  input  [7:0] in_1,
  input  in_2,
  output [7:0] out_3
);

  wire and_1_out, and_2_out, and_3_out, and_4_out, and_5_out, and_6_out, and_7_out, and_8_out;

  and and_1 (and_1_out, in_1[0], in_2);
  and and_2 (and_2_out, in_1[1], in_2);
  and and_3 (and_3_out, in_1[2], in_2);
  and and_4 (and_4_out, in_1[3], in_2);
  and and_5 (and_5_out, in_1[4], in_2);
  and and_6 (and_6_out, in_1[5], in_2);
  and and_7 (and_7_out, in_1[6], in_2);
  and and_8 (and_8_out, in_1[7], in_2);
  assign out_3[0] = in_2 ? and_1_out : 1'bz;  // Controlled_Buffer controlled_buffer_1
  assign out_3[1] = in_2 ? and_2_out : 1'bz;  // Controlled_Buffer controlled_buffer_2
  assign out_3[2] = in_2 ? and_3_out : 1'bz;  // Controlled_Buffer controlled_buffer_3
  assign out_3[3] = in_2 ? and_4_out : 1'bz;  // Controlled_Buffer controlled_buffer_4
  assign out_3[4] = in_2 ? and_5_out : 1'bz;  // Controlled_Buffer controlled_buffer_5
  assign out_3[5] = in_2 ? and_6_out : 1'bz;  // Controlled_Buffer controlled_buffer_6
  assign out_3[6] = in_2 ? and_7_out : 1'bz;  // Controlled_Buffer controlled_buffer_7
  assign out_3[7] = in_2 ? and_8_out : 1'bz;  // Controlled_Buffer controlled_buffer_8
endmodule

module _8_bit_Comparator (
  input  [7:0] in_1,
  input  [7:0] in_2,
  output [7:0] out_3,
  output a__llarger,
  output equal
);

  wire n1_bit_comparator_1_a__larger_2, n1_bit_comparator_1_out_6, n1_bit_comparator_2_a__larger_2,
       n1_bit_comparator_2_out_6, n1_bit_comparator_3_a__larger_2, n1_bit_comparator_3_out_6,
       n1_bit_comparator_4_a__larger_2, n1_bit_comparator_4_out_6, n1_bit_comparator_5_a__larger_2,
       n1_bit_comparator_5_out_6, n1_bit_comparator_6_a__larger_2, n1_bit_comparator_6_out_6,
       n1_bit_comparator_7_a__larger_2, n1_bit_comparator_7_out_6;

  _1_bit_Comparator u_1_bit_comparator_1 (
    .a(in_1[0]), .b(in_2[0]), .c(out_3[0]), .in_1(1'b1), .a__larger(1'b0), .out_6(n1_bit_comparator_1_out_6),
    .a__larger_2(n1_bit_comparator_1_a__larger_2));
  _1_bit_Comparator u_1_bit_comparator_2 (
    .a(in_1[1]), .b(in_2[1]), .c(out_3[1]), .in_1(n1_bit_comparator_1_out_6),
    .a__larger(n1_bit_comparator_1_a__larger_2), .out_6(n1_bit_comparator_2_out_6),
    .a__larger_2(n1_bit_comparator_2_a__larger_2));
  _1_bit_Comparator u_1_bit_comparator_3 (
    .a(in_1[2]), .b(in_2[2]), .c(out_3[2]), .in_1(n1_bit_comparator_2_out_6),
    .a__larger(n1_bit_comparator_2_a__larger_2), .out_6(n1_bit_comparator_3_out_6),
    .a__larger_2(n1_bit_comparator_3_a__larger_2));
  _1_bit_Comparator u_1_bit_comparator_4 (
    .a(in_1[3]), .b(in_2[3]), .c(out_3[3]), .in_1(n1_bit_comparator_3_out_6),
    .a__larger(n1_bit_comparator_3_a__larger_2), .out_6(n1_bit_comparator_4_out_6),
    .a__larger_2(n1_bit_comparator_4_a__larger_2));
  _1_bit_Comparator u_1_bit_comparator_5 (
    .a(in_1[4]), .b(in_2[4]), .c(out_3[4]), .in_1(n1_bit_comparator_4_out_6),
    .a__larger(n1_bit_comparator_4_a__larger_2), .out_6(n1_bit_comparator_5_out_6),
    .a__larger_2(n1_bit_comparator_5_a__larger_2));
  _1_bit_Comparator u_1_bit_comparator_6 (
    .a(in_1[5]), .b(in_2[5]), .c(out_3[5]), .in_1(n1_bit_comparator_5_out_6),
    .a__larger(n1_bit_comparator_5_a__larger_2), .out_6(n1_bit_comparator_6_out_6),
    .a__larger_2(n1_bit_comparator_6_a__larger_2));
  _1_bit_Comparator u_1_bit_comparator_7 (
    .a(in_1[6]), .b(in_2[6]), .c(out_3[6]), .in_1(n1_bit_comparator_6_out_6),
    .a__larger(n1_bit_comparator_6_a__larger_2), .out_6(n1_bit_comparator_7_out_6),
    .a__larger_2(n1_bit_comparator_7_a__larger_2));
  _1_bit_Comparator u_1_bit_comparator_8 (
    .a(in_1[7]), .b(in_2[7]), .c(out_3[7]), .in_1(n1_bit_comparator_7_out_6),
    .a__larger(n1_bit_comparator_7_a__larger_2), .out_6(equal), .a__larger_2(a__llarger));
endmodule

module _1_bit_Comparator (
  input  in_1,
  input  a__larger,
  input  a,
  input  b,
  output c,
  output out_6,
  output a__larger_2
);

  wire and_2_out, not_1_out;

  xor xor_1 (c, a, b);
  not not_1 (not_1_out, c);
  and and_1 (out_6, not_1_out, in_1);
  and and_2 (and_2_out, in_1, a, c);
  or or_1 (a__larger_2, and_2_out, a__larger);

  // Notes on the sheet:
  //   unequal
  //   equal
  //   all bits above equal
  //   all bits equal so far
endmodule

module _3_8_decoder (
  input  in_1,
  input  in_2,
  input  in_3,
  output [7:0] out_4
);

  wire not_1_out, not_2_out, not_3_out;

  not not_1 (not_1_out, in_3);
  not not_2 (not_2_out, in_2);
  not not_3 (not_3_out, in_1);
  and and_1 (out_4[0], not_3_out, not_2_out, not_1_out);
  and and_2 (out_4[1], not_3_out, not_2_out, in_3);
  and and_3 (out_4[2], not_3_out, in_2, not_1_out);
  and and_4 (out_4[3], not_3_out, in_2, in_3);
  and and_5 (out_4[4], in_1, not_2_out, not_1_out);
  and and_6 (out_4[5], in_1, not_2_out, in_3);
  and and_7 (out_4[6], in_1, in_2, not_1_out);
  and and_8 (out_4[7], in_1, in_2, in_3);
endmodule

module XOR_gate (
  input  in_1,
  input  in_2,
  output out_3
);

  wire and_1_out, and_2_out, not_1_out, not_2_out;

  not not_1 (not_1_out, in_1);
  not not_2 (not_2_out, in_2);
  and and_1 (and_1_out, not_1_out, in_2);
  and and_2 (and_2_out, in_1, not_2_out);
  or or_1 (out_3, and_1_out, and_2_out);
endmodule

module SHR (
  input  [7:0] in_1,
  input  in_2,
  output out_3,
  output [7:0] out_4
);

  wire [7:1] register_1_out_5;

  Register register_1 (.in_1(in_1), .out_5({register_1_out_5, out_3}), .S(1'b1), .E(1'b1));  // open: out_4
  Register register_2 (.in_1({in_2, register_1_out_5}), .out_5(out_4), .S(1'b1), .E(1'b1));  // open: out_4
endmodule

module SHL (
  input  in_1,
  input  [7:0] in_2,
  output [7:0] out_3,
  output out_4
);

  wire [6:0] register_1_out_5;

  Register register_1 (.in_1(in_2), .out_5({out_4, register_1_out_5}), .S(1'b1), .E(1'b1));  // open: out_4
  Register register_2 (.in_1({register_1_out_5, in_1}), .out_5(out_3), .S(1'b1), .E(1'b1));  // open: out_4
endmodule

module _8_bit_NOTer (
  input  [7:0] in_1,
  output [7:0] out_2
);

  not not_1 (out_2[0], in_1[0]);
  not not_2 (out_2[1], in_1[1]);
  not not_3 (out_2[2], in_1[2]);
  not not_4 (out_2[3], in_1[3]);
  not not_5 (out_2[4], in_1[4]);
  not not_6 (out_2[5], in_1[5]);
  not not_7 (out_2[6], in_1[6]);
  not not_8 (out_2[7], in_1[7]);
endmodule

module _8_bit_ANDer (
  input  [7:0] in_1,
  input  [7:0] in_2,
  output [7:0] out_3
);

  and and_1 (out_3[0], in_1[0], in_2[0]);
  and and_2 (out_3[1], in_1[1], in_2[1]);
  and and_3 (out_3[2], in_1[2], in_2[2]);
  and and_4 (out_3[3], in_1[3], in_2[3]);
  and and_5 (out_3[4], in_1[4], in_2[4]);
  and and_6 (out_3[5], in_1[5], in_2[5]);
  and and_7 (out_3[6], in_1[6], in_2[6]);
  and and_8 (out_3[7], in_1[7], in_2[7]);
endmodule

module _8_bit_ORer (
  input  [7:0] in_1,
  input  [7:0] in_2,
  output [7:0] out_3
);

  or or_1 (out_3[0], in_1[0], in_2[0]);
  or or_2 (out_3[1], in_1[1], in_2[1]);
  or or_3 (out_3[2], in_1[2], in_2[2]);
  or or_4 (out_3[3], in_1[3], in_2[3]);
  or or_5 (out_3[4], in_1[4], in_2[4]);
  or or_6 (out_3[5], in_1[5], in_2[5]);
  or or_7 (out_3[6], in_1[6], in_2[6]);
  or or_8 (out_3[7], in_1[7], in_2[7]);
endmodule

module _8_bit_ZeroFunction (
  input  [7:0] in_1,
  output out_2
);

  wire or_1_out;

  or or_1 (or_1_out, in_1[0], in_1[1], in_1[2], in_1[3], in_1[4], in_1[5], in_1[6], in_1[7]);
  not not_1 (out_2, or_1_out);
endmodule

module ALU (
  input  [7:0] in_1,
  input  [7:0] in_2,
  input  carry_in,
  input  in_4,
  input  in_5,
  input  in_6,
  output out_7,
  output out_8,
  output out_9,
  output [7:0] out_10,
  output out_11
);

  wire and_1_out, and_2_out, and_3_out, n8_bit_adder_1_carry_out, shl_1_out_4, shr_1_out_3;
  wire [7:0] n3_8_decoder_1_out_4, n8_bit_adder_1_out_5, n8_bit_ander_1_out_3, n8_bit_comparator_1_out_3,
       n8_bit_noter_1_out_2, n8_bit_orer_1_out_3, shl_1_out_3, shr_1_out_4;

  _8_bit_Comparator u_8_bit_comparator_1 (
    .in_1(in_1), .in_2(in_2), .out_3(n8_bit_comparator_1_out_3), .a__llarger(out_7), .equal(out_8));
  _8_bit_ORer u_8_bit_orer_1 (.in_1(in_1), .in_2(in_2), .out_3(n8_bit_orer_1_out_3));
  _8_bit_ANDer u_8_bit_ander_1 (.in_1(in_1), .in_2(in_2), .out_3(n8_bit_ander_1_out_3));
  _8_bit_NOTer u_8_bit_noter_1 (.in_1(in_1), .out_2(n8_bit_noter_1_out_2));
  SHL shl_1 (.in_2(in_1), .out_3(shl_1_out_3), .in_1(carry_in), .out_4(shl_1_out_4));
  SHR shr_1 (.in_1(in_1), .out_4(shr_1_out_4), .out_3(shr_1_out_3), .in_2(carry_in));
  _8_bit_adder u_8_bit_adder_1 (
    .A(in_1), .B(in_2), .out_5(n8_bit_adder_1_out_5), .Carry_out(n8_bit_adder_1_carry_out),
    .Carry_in(carry_in));
  _3_8_decoder u_3_8_decoder_1 (.in_1(in_6), .in_2(in_5), .in_3(in_4), .out_4(n3_8_decoder_1_out_4));
  smallEnable smallenable_1 (.in_1(n8_bit_comparator_1_out_3), .out_3(out_10), .in_2(n3_8_decoder_1_out_4[6]));
  smallEnable smallenable_2 (.in_1(n8_bit_orer_1_out_3), .out_3(out_10), .in_2(n3_8_decoder_1_out_4[5]));
  smallEnable smallenable_3 (.in_1(n8_bit_ander_1_out_3), .out_3(out_10), .in_2(n3_8_decoder_1_out_4[4]));
  smallEnable smallenable_4 (.in_1(n8_bit_noter_1_out_2), .out_3(out_10), .in_2(n3_8_decoder_1_out_4[3]));
  smallEnable smallenable_5 (.in_1(shl_1_out_3), .out_3(out_10), .in_2(n3_8_decoder_1_out_4[2]));
  smallEnable smallenable_6 (.in_1(shr_1_out_4), .out_3(out_10), .in_2(n3_8_decoder_1_out_4[1]));
  smallEnable smallenable_7 (.in_1(n8_bit_adder_1_out_5), .out_3(out_10), .in_2(n3_8_decoder_1_out_4[0]));
  and and_1 (and_1_out, shl_1_out_4, n3_8_decoder_1_out_4[2]);
  and and_2 (and_2_out, shr_1_out_3, n3_8_decoder_1_out_4[1]);
  and and_3 (and_3_out, n8_bit_adder_1_carry_out, n3_8_decoder_1_out_4[0]);
  assign out_11 = n3_8_decoder_1_out_4[2] ? and_1_out : 1'bz;  // Controlled_Buffer controlled_buffer_1
  assign out_11 = n3_8_decoder_1_out_4[1] ? and_2_out : 1'bz;  // Controlled_Buffer controlled_buffer_2
  assign out_11 = n3_8_decoder_1_out_4[0] ? and_3_out : 1'bz;  // Controlled_Buffer controlled_buffer_3
  _8_bit_ZeroFunction u_8_bit_zerofunction_1 (.in_1(out_10), .out_2(out_9));

  // Notes on the sheet:
  //   a
  //   b
endmodule

module Clock (
  input  in_1,
  output clk,
  output clk_set,
  output clk_enable
);

  wire j_k_ff_1_qn, nand_1_out;

  J_K_Flip_Flop j_k_ff_1 (.J(1'b1), .clk(in_1), .K(1'b1), .Q(clk), .Qn(j_k_ff_1_qn));  // open: preset, en, reset
  nand nand_1 (nand_1_out, in_1, clk);
  nand nand_2 (clk_enable, j_k_ff_1_qn, in_1);
  not not_1 (clk_set, nand_1_out);
endmodule

module J_K_flip_flop (
  input  J,
  input  K,
  output Q,
  output Q_prime
);

  wire clock_1_out, nand_1_out, nand_2_out;

  Clock_part clock_1 (.out(clock_1_out));
  nand nand_1 (nand_1_out, Q_prime, J, clock_1_out);
  nand nand_2 (nand_2_out, clock_1_out, K, Q);
  nand nand_3 (Q, nand_1_out, Q_prime);
  nand nand_4 (Q_prime, Q, nand_2_out);
endmodule

module Stepper (
  input  in_1,
  input  in_2,
  output out_3,
  output out_4,
  output out_5,
  output out_6,
  output out_7,
  output out_8,
  output out_9
);

  wire m_1_out_3, m_2_out_3, m_3_out_3, m_4_out_3, m_5_out_3, m_6_out_3, m_7_out_3, m_8_out_3, m_9_out_3,
       m_10_out_3, m_11_out_3, not_1_out, not_2_out, not_3_out, not_4_out, not_5_out, not_6_out, not_7_out,
       not_8_out, or_1_out, or_2_out;

  not not_1 (not_1_out, in_2);
  not not_2 (not_2_out, in_1);
  or or_1 (or_1_out, in_1, not_1_out);
  or or_2 (or_2_out, in_1, in_2);
  or or_3 (out_3, in_1, not_3_out);
  not not_3 (not_3_out, m_2_out_3);
  M m_1 (.S(not_2_out), .E(or_1_out), .out_3(m_1_out_3));
  M m_2 (.S(m_1_out_3), .E(or_2_out), .out_3(m_2_out_3));
  and and_1 (out_4, m_2_out_3, not_4_out);
  M m_3 (.S(m_2_out_3), .E(or_1_out), .out_3(m_3_out_3));
  not not_4 (not_4_out, m_4_out_3);
  M m_4 (.S(m_3_out_3), .E(or_2_out), .out_3(m_4_out_3));
  and and_2 (out_5, m_4_out_3, not_5_out);
  M m_5 (.S(m_4_out_3), .E(or_1_out), .out_3(m_5_out_3));
  not not_5 (not_5_out, m_6_out_3);
  M m_6 (.S(m_5_out_3), .E(or_2_out), .out_3(m_6_out_3));
  and and_3 (out_6, m_6_out_3, not_6_out);
  M m_7 (.S(m_6_out_3), .E(or_1_out), .out_3(m_7_out_3));
  not not_6 (not_6_out, m_8_out_3);
  M m_8 (.S(m_7_out_3), .E(or_2_out), .out_3(m_8_out_3));
  and and_4 (out_7, m_8_out_3, not_7_out);
  not not_7 (not_7_out, m_10_out_3);
  M m_9 (.S(m_8_out_3), .E(or_1_out), .out_3(m_9_out_3));
  M m_10 (.S(m_9_out_3), .E(or_2_out), .out_3(m_10_out_3));
  and and_5 (out_8, m_10_out_3, not_8_out);
  not not_8 (not_8_out, out_9);
  M m_11 (.S(m_10_out_3), .E(or_1_out), .out_3(m_11_out_3));
  M m_12 (.S(m_11_out_3), .E(or_2_out), .out_3(out_9));
endmodule

module Control_section (
  input  clks,
  input  clk,
  input  clke,
  output MAR,
  output RAM,
  output ACC,
  output ACC_2,
  output RAM_2,
  output R0,
  output TMP,
  output R1,
  output R0_2,
  output R2,
  output R1_2,
  output R2_2,
  output R2_3,
  output R3
);

  wire stepper_1_out_6, stepper_1_out_7, stepper_1_out_8, stepper_1_out_9;

  and and_1 (RAM, clke, 1'b0);
  and and_2 (ACC_2, clke, stepper_1_out_8);
  and and_3 (R0, clke, stepper_1_out_7);
  and and_4 (R1, clke, 1'b0);
  and and_5 (R2, clke, stepper_1_out_6);
  and and_6 (R2_2, clke, 1'b0);
  Stepper stepper_1 (
    .in_1(stepper_1_out_9), .in_2(clk), .out_6(stepper_1_out_6), .out_7(stepper_1_out_7),
    .out_8(stepper_1_out_8), .out_9(stepper_1_out_9));  // open: out_3, out_4, out_5
  and and_7 (MAR, clks, 1'b0);
  and and_8 (ACC, clks, stepper_1_out_7);
  and and_9 (RAM_2, clks, 1'b0);
  and and_10 (TMP, clks, stepper_1_out_6);
  and and_11 (R0_2, clks, 1'b0);
  and and_12 (R1_2, clks, 1'b0);
  and and_13 (R2_3, clks, 1'b0);
  and and_14 (R3, clks, stepper_1_out_8);

  // Notes on the sheet:
  //   All Enables
  //   All sets
endmodule

module M (
  input  S,
  input  E,
  output out_3
);

  wire nand_1_out, nand_2_out, nand_4_out;

  nand nand_1 (nand_1_out, S, E);
  nand nand_2 (nand_2_out, E, nand_1_out);
  nand nand_3 (out_3, nand_1_out, nand_4_out);
  nand nand_4 (nand_4_out, out_3, nand_2_out);
endmodule

module CPU (
);

  ALU alu_1 ();  // open: in_1, in_2, carry_in, out_10, out_9, out_8, out_7, out_11, in_4, in_5, in_6
  _256_byte_RAM u_256_byte_ram_1 ();  // open: out_6, Reset, in_5, Address, R, W
endmodule
